# Fritzing sketch geocaching (saved by Fritzing 0.9.1b)
circuit board: 8.46667cm x 5.64444cm
breadboards: 2

parts:
  S4 = Pushbutton [package="[THT]"]
  S3 = Pushbutton [package="[THT]"]
  S2 = Pushbutton [package="[THT]"]
  S1 = Pushbutton [package="[THT]"]
  R1 = Resistor [tolerance=±5% resistance=10k package=THT]
  R2 = Resistor [tolerance=±5% resistance=10k package=THT]
  R4 = Resistor [tolerance=±5% resistance=10k package=THT]
  R3 = Resistor [tolerance=±5% resistance=10k package=THT]
  Bauteil1 = Arduino Uno (Rev3)
  LED1 = RGB LED (com. cathode, rgb) [package="5 mm [THT]"]
  LED2 = LED - 5mm [color="Blue (430nm)" package="5 mm [THT]"]
  LED3 = LED - 5mm [color="Yellow (595nm)" package="5 mm [THT]"]
  R7 = Resistor [tolerance=±5% resistance=220 package=THT]
  R8 = Resistor [tolerance=±5% resistance=220 package=THT]
  R9 = Resistor [tolerance=±5% resistance=220 package=THT]
  R10 = Resistor [tolerance=±5% resistance=220 package=THT]
  LCD1 = LCD screen
  R11 = TRIMPOT [package=3362u-2]
  R12 = Resistor [tolerance=±5% resistance=220 package=THT]

nets:
  N1: S4.Pin_1, S4.Pin_2, R4.Pin_0, Bauteil1.A4/SDA
  5V: S4.Pin_3, S4.Pin_4, S3.Pin_3, S3.Pin_4, S2.Pin_3, S2.Pin_4, S1.Pin_3, S1.Pin_4, Bauteil1.5V, LCD1.VDD, R11.CCW
  N2: S3.Pin_1, S3.Pin_2, R3.Pin_0, Bauteil1.A3
  N3: S2.Pin_1, S2.Pin_2, R2.Pin_0, Bauteil1.A2
  N4: S1.Pin_1, S1.Pin_2, R1.Pin_0, Bauteil1.A1
  GND: R1.Pin_1, R2.Pin_1, R4.Pin_1, R3.Pin_1, Bauteil1.GND, LED1.common_cathode, LED2.cathode, LED3.cathode, LCD1.VSS, LCD1.R/W, LCD1.LED-, R11.CW
  N5: Bauteil1.A0, R12.Pin_0
  N6: Bauteil1.D8, R8.Pin_0
  N7: Bauteil1.D9_PWM, R7.Pin_1
  N8: Bauteil1.D10_PWM/SS, R10.Pin_1
  N9: Bauteil1.D11_PWM/MOSI, LCD1.E
  N10: Bauteil1.D12/MISO, LCD1.RS
  N11: Bauteil1.D2, LCD1.DB7
  N12: Bauteil1.D3_PWM, LCD1.DB6
  N13: Bauteil1.D4, LCD1.DB5
  N14: Bauteil1.D5_PWM, LCD1.DB4
  N15: Bauteil1.D7, R9.Pin_1
  N16: LED1.red_anode, R8.Pin_1
  N17: LED1.blue_anode, R7.Pin_0
  N18: LED2.anode, R10.Pin_0
  N19: LED3.anode, R9.Pin_0
  N20: LCD1.V0, R11.WIPER
  N21: LCD1.LED+, R12.Pin_1
